# Fritzing sketch tkpower (saved by Fritzing 0.9.2b)
circuit board: 8.46667cm x 5.64444cm
breadboards: 1

parts:
  Part1 = Pro Trinket 5V
  R1 = Resistor [tolerance=±5% resistance=33 package=THT]
  J4 = Screw terminal - 2 pins [package=THT]
  U1 = Voltage Regulator [package=to220-adj]
  R4 = Resistor [tolerance=±5% resistance=470 package=THT]
  R5 = Resistor [tolerance=±5% resistance=470 package=THT]
  C1 = Electrolytic Capacitor [capacitance=1µF package="100 mil [THT, electrolytic]"]

nets:
  5V: Part1.VBAT, U1.IN
  GND: Part1.GND, R5.Pin_1, C1.-
  N1: Part1.A0, R1.Pin_1, J4.pin2
  N2: R1.Pin_0, J4.pin1, U1.OUT, R4.Pin_1, C1.+
  N3: U1.ADJ, R4.Pin_0, R5.Pin_0

notes:
  Current Clamp connects to J4

custom parts:
  Pro Trinket 5V: The Pro Trinket 5V is like an Arduino Pro Mini with more pins and USB included. Built with the common core Arduino chip, the ATmega328p, it has 18 GPIO, 2 extra analog inputs, 28K of flash, and 2K of RAM. It has onboard USB bootloading support with Optiboot support, so you can either program your Pro Trinket over USB or with a FTDI cable. The Pro Trinket is programmable using the Arduino IDE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

// code stored in the sketch: tkpower.foo.ino
// EmonLibrary examples openenergymonitor.org, Licence GNU GPL V3

#include "EmonLib.h"                   // Include Emon Library
EnergyMonitor emon1;                   // Create an instance
EnergyMonitor emon0;

void setup()
{
  Serial.begin(9600);

  emon1.current(1, 90.91);             // Current: input pin, calibration.
  emon0.current(0, 90.91);
}

void loop()
{
  double Irms1 = emon1.calcIrms(5920);  // Calculate Irms only
  double Irms0 = emon0.calcIrms(5920);
  Serial.print ("pin1 ");
  Serial.print(Irms1*122.0);         // Apparent power
  Serial.print(" ");
  Serial.print(Irms1);
  Serial.print(" ");
  Serial.print("pin0 ");
  Serial.print(Irms0*122.0);         // Apparent power
  Serial.print(" ");
  Serial.print(Irms0);
  Serial.print(" ");
  Serial.print((Irms0*122.0)+(Irms1*122.0));
  Serial.print(" ");
  Serial.println(Irms0+Irms1);
  
 

}
